// Logisim project cell.circ as structural Verilog: 1 circuit, main circuit cell
module \cell  (
  input  a,
  input  b,
  input  cin,
  input  [2:0] sel,
  output S,
  output Cout
);

  wire adder_1_cout, adder_1_out, and_2_out, AND_out, NOT_A_out, NOT_B_out, OR_out, subtractor_1_bout,
       subtractor_1_out, XOR_out;

  and AND (AND_out, a, b);
  or OR (OR_out, a, b);
  nor XOR (XOR_out, a, a);
  not NOT_A (NOT_A_out, a);
  not NOT_B (NOT_B_out, b);
  Adder #(.width(1)) adder_1 (.a(a), .b(b), .out(adder_1_out), .cin(cin), .cout(adder_1_cout));
  Subtractor #(.width(1)) subtractor_1 (.a(a), .b(b), .out(subtractor_1_out), .bin(cin), .bout(subtractor_1_bout));
  and and_2 (and_2_out, sel[2], ~sel[1], ~sel[0]);  // AND_Gate
  Multiplexer #(.enable("false")) multiplexer_1 (
    .in0(subtractor_1_bout), .in1(adder_1_cout), .out(Cout), .sel(and_2_out));
  Multiplexer #(.select(3), .enable("false")) multiplexer_2 (
    .in0(AND_out), .in1(OR_out), .in2(XOR_out), .in3(NOT_A_out), .in4(NOT_B_out), .in5(adder_1_out),
    .in6(subtractor_1_out), .out(S), .sel(sel));  // open: in7

  // Notes on the sheet:
  //   AND = 000
  //   OR = 001
  //   XOR = 010
  //   NOT A = 011
  //   NOT B = 100
  //   SUM = 101
  //   SUB = 110
endmodule
