// Logisim project square_root.circ as structural Verilog
module main (
  input  [7:0] Entrada_X,
  output [7:0] out_2
);

  wire CLK_out, comparator_1_eq, comparator_1_gt, comparator_1_lt, SEL_out;
  wire [7:0] adder_1_out, adder_2_out, adder_3_out, adder_4_out, multiplexer_1_out, multiplexer_3_out,
       multiplexer_4_out, Reg_D_q, Reg_R_q, Reg_S_q;

  Multiplexer #(.width(8), .enable("false")) multiplexer_1 (
    .in0(adder_1_out), .in1(8'h1), .out(multiplexer_1_out), .sel(SEL_out));
  Register Reg_R (.D(multiplexer_1_out), .Q(Reg_R_q), .clk(CLK_out));  // open: en, clr
  Multiplexer #(.width(8), .enable("false")) multiplexer_2 (
    .in0({8{1'b0}}), .in1(adder_1_out), .out(out_2), .sel(comparator_1_lt));
  Adder adder_1 (.a(Reg_R_q), .b(8'h1), .out(adder_1_out));  // open: cin, cout
  Multiplexer #(.width(8), .enable("false")) multiplexer_3 (
    .in0(adder_2_out), .in1(8'h2), .out(multiplexer_3_out), .sel(SEL_out));
  Clock CLK (.out(CLK_out));
  Register Reg_D (.D(multiplexer_3_out), .Q(Reg_D_q), .clk(CLK_out));  // open: en, clr
  Clock SEL (.out(SEL_out));
  Adder adder_2 (.a(Reg_D_q), .b(8'h2), .out(adder_2_out));  // open: cin, cout
  Multiplexer #(.width(8), .enable("false")) multiplexer_4 (
    .in0(adder_4_out), .in1(8'h4), .out(multiplexer_4_out), .sel(SEL_out));
  Adder adder_3 (.a(adder_2_out), .b(8'h1), .out(adder_3_out));  // open: cin, cout
  Comparator comparator_1 (
    .a(Entrada_X), .b(adder_4_out), .gt(comparator_1_gt), .eq(comparator_1_eq), .lt(comparator_1_lt));
  Register Reg_S (.D(multiplexer_4_out), .Q(Reg_S_q), .clk(CLK_out));  // open: en, clr
  Adder adder_4 (.a(Reg_S_q), .b(adder_3_out), .out(adder_4_out));  // open: cin, cout

  // Notes on the sheet:
  //   r+1
  //   CONTROLE
  //   enquanto t = 1
  //   d+2
  //   4 ou (s+d+1)
  //   d+1
  //   s > x
  //   s+d+1
endmodule

module square_root (
  input  [7:0] Entrada_X,
  output [7:0] out_2
);

  wire CLK_out, clock_1_out, clock_2_out, comparator_1_eq, comparator_1_gt, comparator_1_lt;
  wire [7:0] adder_2_out, adder_3_out, adder_4_out, multiplexer_1_out, multiplexer_2_out, multiplexer_3_out,
       multiplexer_4_out, Reg_D_q, Reg_R_q, Reg_S_q;

  Multiplexer #(.width(8), .enable("false")) multiplexer_1 (
    .in0(out_2), .in1(8'h1), .out(multiplexer_1_out), .sel(CLK_out));
  Register Reg_R (.D(multiplexer_1_out), .Q(Reg_R_q), .clk(CLK_out));  // open: en, clr
  Adder adder_1 (.a(Reg_R_q), .b(8'h1), .out(out_2));  // open: cin, cout
  Multiplexer #(.width(8), .enable("false")) multiplexer_2 (
    .in0(adder_2_out), .in1({8{1'b0}}), .out(multiplexer_2_out), .sel(CLK_out));
  Clock CLK (.out(CLK_out));
  Register Reg_D (.D(multiplexer_2_out), .Q(Reg_D_q), .clk(CLK_out));  // open: en, clr
  Clock clock_1 (.out(clock_1_out));
  Clock clock_2 (.out(clock_2_out));
  Adder adder_2 (.a(Reg_D_q), .b(8'h2), .out(adder_2_out));  // open: cin, cout
  Multiplexer #(.width(8), .enable("false")) multiplexer_3 (
    .in0(adder_4_out), .in1({8{1'b0}}), .out(multiplexer_3_out), .sel(CLK_out));
  Adder adder_3 (.a(adder_2_out), .b(8'h1), .out(adder_3_out));  // open: cin, cout
  Comparator comparator_1 (
    .a(Entrada_X), .b(adder_4_out), .gt(comparator_1_gt), .eq(comparator_1_eq), .lt(comparator_1_lt));
  Register Reg_S (.D(multiplexer_3_out), .Q(Reg_S_q), .clk(CLK_out));  // open: en, clr
  Multiplexer #(.width(8)) multiplexer_4 (
    .in0(8'h4), .in1(adder_3_out), .out(multiplexer_4_out), .sel(clock_1_out), .en(clock_2_out));
  Adder adder_4 (.a(Reg_S_q), .b(multiplexer_4_out), .out(adder_4_out));  // open: cin, cout

  // Notes on the sheet:
  //   r+1
  //   CONTROLE
  //   enquanto t = 1
  //   01 = 4
  //   11 = (d+1)
  //   d+2
  //   d+1
  //   s > x
  //   4 ou (d+1)
  //   s+d+1
endmodule
